// Logisim project Guia_0501.circ as structural Verilog: 1 circuit, main circuit main
module main (
  input  in_1,
  input  in_2
);

  wire nor_1_out;

  nor nor_1 (nor_1_out, in_1, in_2);
  // Probe on nor_1_out

  // Notes on the sheet:
  //   Guia0501 Arthur Goncalves de Moraes 816479
endmodule
