// Logisim project Guia_0502.circ as structural Verilog: 1 circuit, main circuit main
module main (
  input  in_1,
  input  in_2
);

  wire nand_1_out, nand_2_out, nand_3_out, nand_4_out;

  nand nand_1 (nand_1_out, 1'b1, in_1);
  nand nand_2 (nand_2_out, in_2, in_2);
  nand nand_3 (nand_3_out, nand_2_out, 1'b1);
  nand nand_4 (nand_4_out, nand_1_out, nand_3_out);
  // Probe on nand_4_out

  // Notes on the sheet:
  //   G0502 Arthur Goncalves de Moraes 816479
endmodule
