// Logisim project Guia_0504.circ as structural Verilog: 1 circuit, main circuit main
module main (
  input  in_1,
  input  in_2
);

  wire nand_1_out, nand_2_out;

  nand nand_1 (nand_1_out, in_1, in_1);
  nand nand_2 (nand_2_out, nand_1_out, in_2);
  // Probe on nand_2_out

  // Notes on the sheet:
  //   G0504 Arthur Goncalves de Moraes 816479
endmodule
