// Logisim project R0103a.circ as structural Verilog: 1 circuit, main circuit main
module main (
  input  a,
  input  b
);

  wire nand_1_out, nand_2_out, nor_1_out;

  nor nor_1 (nor_1_out, a, a);
  nand nand_1 (nand_1_out, nor_1_out, b);
  nand nand_2 (nand_2_out, nand_1_out, nand_1_out);
  // Probe on nand_2_out

  // Notes on the sheet:
  //   Arthur Goncalves de Moraes 816479 - q3a
endmodule
