// Logisim project q4a.circ as structural Verilog: 1 circuit, main circuit main
module main (
  input  a,
  input  b,
  input  c
);

  wire and_1_out, not_1_out, not_2_out;

  not not_1 (not_1_out, a);
  not not_2 (not_2_out, c);
  and and_1 (and_1_out, not_1_out, not_2_out);
  // Probe on and_1_out

  // Notes on the sheet:
  //   Arthur Goncalves de Moraes 816479 q4a
endmodule
