// Logisim project q4d.circ as structural Verilog: 1 circuit, main circuit main
module main (
  input  a,
  input  b,
  input  c
);

  wire and_1_out, and_2_out, and_3_out, and_4_out, not_1_out, not_2_out, not_3_out, or_1_out;

  not not_1 (not_1_out, b);
  not not_2 (not_2_out, a);
  not not_3 (not_3_out, c);
  and and_1 (and_1_out, not_1_out, c);
  and and_2 (and_2_out, not_2_out, b, c);
  and and_3 (and_3_out, a, b, not_3_out);
  or or_1 (or_1_out, and_2_out, and_3_out);
  and and_4 (and_4_out, or_1_out, and_1_out);
  // Probe on and_4_out

  // Notes on the sheet:
  //   Arthur Goncalves de Moraes 816479 q4d
endmodule
