// Logisim project EP_01.circ as structural Verilog: 6 circuits, main circuit main
module main (
  input  a0,
  input  a1,
  input  a2,
  input  in_4,
  input  a3,
  input  b0,
  input  b1,
  input  b2,
  input  b3,
  output S0,
  output S1,
  output S2,
  output S3,
  output Co,
  output overflow
);

  wire displaydecoder_1_p5, displaydecoder_1_p6, displaydecoder_1_p7, displaydecoder_1_p8,
       displaydecoder_1_p9, displaydecoder_1_p10, displaydecoder_1_p11, displaydecoder_2_p5,
       displaydecoder_2_p6, displaydecoder_2_p7, displaydecoder_2_p8, displaydecoder_2_p9,
       displaydecoder_2_p10, displaydecoder_2_p11, displaydecoder_3_p5, displaydecoder_3_p6,
       displaydecoder_3_p7, displaydecoder_3_p8, displaydecoder_3_p9, displaydecoder_3_p10,
       displaydecoder_3_p11;

  soma4bits soma4bits_1 (
    .a1(a0), .a2(a1), .a3(a2), .a4(a3), .b1(b0), .b2(b1), .b3(b2), .b4(b3), .carry_in(in_4), .carry_out(Co),
    .S0(S0), .S1(S1), .S2(S2), .S3(S3), .overflow(overflow));
  _7_Segment_Display u_7_segment_display_1 (
    .g(displaydecoder_1_p11), .f(displaydecoder_1_p10), .a(displaydecoder_1_p5), .b(displaydecoder_1_p6),
    .e(displaydecoder_1_p9), .d(displaydecoder_1_p8), .c(displaydecoder_1_p7));  // open: dp
  // DisplayDecoder #(.multibit("false")) displaydecoder_1: pin names not known; wires that end beside it: a0, a1, a2, a3, displaydecoder_1_p5, displaydecoder_1_p6, displaydecoder_1_p7, displaydecoder_1_p8, displaydecoder_1_p9, displaydecoder_1_p10, displaydecoder_1_p11
  _7_Segment_Display u_7_segment_display_2 (
    .g(displaydecoder_2_p11), .f(displaydecoder_2_p10), .a(displaydecoder_2_p5), .b(displaydecoder_2_p6),
    .e(displaydecoder_2_p9), .d(displaydecoder_2_p8), .c(displaydecoder_2_p7));  // open: dp
  // DisplayDecoder #(.multibit("false")) displaydecoder_2: pin names not known; wires that end beside it: b0, b1, b2, b3, displaydecoder_2_p5, displaydecoder_2_p6, displaydecoder_2_p7, displaydecoder_2_p8, displaydecoder_2_p9, displaydecoder_2_p10, displaydecoder_2_p11
  // DisplayDecoder #(.multibit("false")) displaydecoder_3: pin names not known; wires that end beside it: S0, S1, S2, S3, displaydecoder_3_p5, displaydecoder_3_p6, displaydecoder_3_p7, displaydecoder_3_p8, displaydecoder_3_p9, displaydecoder_3_p10, displaydecoder_3_p11
  _7_Segment_Display u_7_segment_display_3 (
    .g(displaydecoder_3_p11), .f(displaydecoder_3_p10), .a(displaydecoder_3_p5), .b(displaydecoder_3_p6),
    .e(displaydecoder_3_p9), .d(displaydecoder_3_p8), .c(displaydecoder_3_p7));  // open: dp
endmodule

module somaCompleta (
  input  a,
  input  b,
  input  carry_in,
  output S,
  output carry_out
);

  wire meiasoma_1_carry_out, meiasoma_1_s, meiasoma_2_carry_out;

  meiaSoma meiasoma_1 (.a(b), .b(a), .Carry_Out(meiasoma_1_carry_out), .S(meiasoma_1_s));
  meiaSoma meiasoma_2 (.a(meiasoma_1_s), .b(carry_in), .Carry_Out(meiasoma_2_carry_out), .S(S));
  or or_1 (carry_out, meiasoma_2_carry_out, meiasoma_1_carry_out);
endmodule

module soma4bits (
  input  a1,
  input  a2,
  input  a3,
  input  a4,
  input  b1,
  input  b2,
  input  b3,
  input  b4,
  input  carry_in,
  output S0,
  output S1,
  output S2,
  output S3,
  output carry_out,
  output overflow
);

  wire soma2bits_1_carry_out;

  soma2bits soma2bits_1 (
    .a1(a1), .a2(a2), .b1(b1), .b2(b2), .carry_in(carry_in), .carry_out(soma2bits_1_carry_out), .S0(S0),
    .S1(S1));
  soma2bits soma2bits_2 (
    .a1(a3), .a2(a4), .b1(b3), .b2(b4), .carry_in(soma2bits_1_carry_out), .carry_out(carry_out), .S0(S2),
    .S1(S3));

  assign overflow = carry_out;
endmodule

module meiaSoma (
  input  a,
  input  b,
  output S,
  output Carry_Out
);

  xor xor_1 (S, a, b);
  and and_1 (Carry_Out, a, b);
endmodule

module soma2bits (
  input  carry_in,
  input  a1,
  input  a2,
  input  b1,
  input  b2,
  output S0,
  output S1,
  output carry_out
);

  wire somacompleta_1_carry_out, somacompleta_1_s, somacompleta_2_carry_out, somacompleta_2_s,
       somacompleta_3_carry_out;

  somaCompleta somacompleta_1 (
    .a(a1), .b(a2), .carry_in(a2), .carry_out(somacompleta_1_carry_out), .S(somacompleta_1_s));
  somaCompleta somacompleta_2 (
    .a(b1), .b(b2), .carry_in(b2), .carry_out(somacompleta_2_carry_out), .S(somacompleta_2_s));
  somaCompleta somacompleta_3 (
    .a(somacompleta_1_s), .b(somacompleta_2_s), .carry_in(carry_in), .carry_out(somacompleta_3_carry_out),
    .S(S0));
  somaCompleta somacompleta_4 (
    .a(somacompleta_2_carry_out), .b(somacompleta_1_carry_out), .carry_in(somacompleta_3_carry_out),
    .carry_out(carry_out), .S(S1));
endmodule

module EP_01 (
  input  a0,
  input  a1,
  input  a2,
  input  Ci,
  input  a3,
  input  b0,
  input  b1,
  input  b2,
  input  b3,
  output S0,
  output S1,
  output S2,
  output S3,
  output Co,
  output overflow
);

  soma4bits soma4bits_1 (
    .a1(a0), .a2(a1), .a3(a2), .a4(a3), .b1(b0), .b2(b1), .b3(b2), .b4(b3), .carry_in(Ci), .carry_out(Co),
    .S0(S0), .S1(S1), .S2(S2), .S3(S3), .overflow(overflow));
endmodule
