// Logisim project EP_01_decode.circ as structural Verilog: 6 circuits, main circuit main
module main (
  input  a0,
  input  a1,
  input  a2,
  input  in_4,
  input  a3,
  input  b0,
  input  b1,
  input  b2,
  input  b3,
  output S0,
  output S1,
  output S2,
  output S3,
  output Co,
  output overflow
);

  wire decodiicador_1_a, decodiicador_1_b, decodiicador_1_c, decodiicador_1_d, decodiicador_1_e,
       decodiicador_1_f, decodiicador_1_g, decodiicador_2_a, decodiicador_2_b, decodiicador_2_c,
       decodiicador_2_d, decodiicador_2_e, decodiicador_2_f, decodiicador_2_g, decodiicador_3_a,
       decodiicador_3_b, decodiicador_3_c, decodiicador_3_d, decodiicador_3_e, decodiicador_3_f,
       decodiicador_3_g;

  decodiicador decodiicador_1 (
    .a3(a3), .a1(a2), .a1_2(a1), .a0(a0), .a(decodiicador_1_a), .b(decodiicador_1_b), .c(decodiicador_1_c),
    .d(decodiicador_1_d), .e(decodiicador_1_e), .f(decodiicador_1_f), .g(decodiicador_1_g));
  soma4bits soma4bits_1 (
    .a1(a0), .a2(a1), .a3(a2), .a4(a3), .b1(b0), .b2(b1), .b3(b2), .b4(b3), .carry_in(in_4), .carry_out(Co),
    .S0(S0), .S1(S1), .S2(S2), .S3(S3), .overflow(overflow));
  decodiicador decodiicador_2 (
    .a3(b3), .a1(b2), .a1_2(b1), .a0(b0), .a(decodiicador_2_a), .b(decodiicador_2_b), .c(decodiicador_2_c),
    .d(decodiicador_2_d), .e(decodiicador_2_e), .f(decodiicador_2_f), .g(decodiicador_2_g));
  _7_Segment_Display u_7_segment_display_1 (
    .g(decodiicador_1_g), .f(decodiicador_1_f), .a(decodiicador_1_a), .b(decodiicador_1_b),
    .e(decodiicador_1_e), .d(decodiicador_1_d), .c(decodiicador_1_c));  // open: dp
  _7_Segment_Display u_7_segment_display_2 (
    .g(decodiicador_2_g), .f(decodiicador_2_f), .a(decodiicador_2_a), .b(decodiicador_2_b),
    .e(decodiicador_2_e), .d(decodiicador_2_d), .c(decodiicador_2_c));  // open: dp
  decodiicador decodiicador_3 (
    .a3(S3), .a1(S2), .a1_2(S1), .a0(S0), .a(decodiicador_3_a), .b(decodiicador_3_b), .c(decodiicador_3_c),
    .d(decodiicador_3_d), .e(decodiicador_3_e), .f(decodiicador_3_f), .g(decodiicador_3_g));
  _7_Segment_Display u_7_segment_display_3 (
    .g(decodiicador_3_g), .f(decodiicador_3_f), .a(decodiicador_3_a), .b(decodiicador_3_b),
    .e(decodiicador_3_e), .d(decodiicador_3_d), .c(decodiicador_3_c));  // open: dp
endmodule

module somaCompleta (
  input  a,
  input  b,
  input  carry_in,
  output S,
  output carry_out
);

  wire meiasoma_1_carry_out, meiasoma_1_s, meiasoma_2_carry_out;

  meiaSoma meiasoma_1 (.a(b), .b(a), .Carry_Out(meiasoma_1_carry_out), .S(meiasoma_1_s));
  meiaSoma meiasoma_2 (.a(meiasoma_1_s), .b(carry_in), .Carry_Out(meiasoma_2_carry_out), .S(S));
  or or_1 (carry_out, meiasoma_2_carry_out, meiasoma_1_carry_out);
endmodule

module soma4bits (
  input  a1,
  input  a2,
  input  a3,
  input  a4,
  input  b1,
  input  b2,
  input  b3,
  input  b4,
  input  carry_in,
  output S0,
  output S1,
  output S2,
  output S3,
  output carry_out,
  output overflow
);

  wire soma2bits_1_carry_out;

  soma2bits soma2bits_1 (
    .a1(a1), .a2(a2), .b1(b1), .b2(b2), .carry_in(carry_in), .carry_out(soma2bits_1_carry_out), .S0(S0),
    .S1(S1));
  soma2bits soma2bits_2 (
    .a1(a3), .a2(a4), .b1(b3), .b2(b4), .carry_in(soma2bits_1_carry_out), .carry_out(carry_out), .S0(S2),
    .S1(S3));

  assign overflow = carry_out;
endmodule

module meiaSoma (
  input  a,
  input  b,
  output S,
  output Carry_Out
);

  xor xor_1 (S, a, b);
  and and_1 (Carry_Out, a, b);
endmodule

module soma2bits (
  input  carry_in,
  input  a1,
  input  a2,
  input  b1,
  input  b2,
  output S0,
  output S1,
  output carry_out
);

  wire somacompleta_1_carry_out, somacompleta_1_s, somacompleta_2_carry_out, somacompleta_2_s,
       somacompleta_3_carry_out;

  somaCompleta somacompleta_1 (
    .a(a1), .b(a2), .carry_in(a2), .carry_out(somacompleta_1_carry_out), .S(somacompleta_1_s));
  somaCompleta somacompleta_2 (
    .a(b1), .b(b2), .carry_in(b2), .carry_out(somacompleta_2_carry_out), .S(somacompleta_2_s));
  somaCompleta somacompleta_3 (
    .a(somacompleta_1_s), .b(somacompleta_2_s), .carry_in(carry_in), .carry_out(somacompleta_3_carry_out),
    .S(S0));
  somaCompleta somacompleta_4 (
    .a(somacompleta_2_carry_out), .b(somacompleta_1_carry_out), .carry_in(somacompleta_3_carry_out),
    .carry_out(carry_out), .S(S1));
endmodule

module decodiicador (
  input  a3,
  input  a1,
  input  a1_2,
  input  a0,
  output a,
  output b,
  output c,
  output d,
  output e,
  output f,
  output g
);

  wire and_1_out, and_2_out, and_3_out, and_4_out, and_5_out, and_6_out, and_7_out, and_8_out, and_9_out,
       and_10_out, and_11_out, and_12_out, and_13_out, and_14_out, and_15_out, and_16_out, and_17_out,
       and_18_out, and_19_out, and_20_out, and_21_out, and_22_out, and_23_out, and_24_out, and_25_out,
       and_26_out, and_27_out, and_28_out, and_29_out, and_30_out, and_31_out, and_32_out, and_33_out,
       and_34_out, and_35_out, not_1_out, not_2_out, not_3_out, not_4_out, not_5_out, not_6_out, not_7_out,
       not_8_out, not_9_out, not_10_out, not_11_out, not_12_out, not_13_out, not_14_out, not_15_out,
       not_16_out, not_17_out, not_18_out, not_19_out, not_20_out, not_21_out, not_22_out, not_23_out,
       not_24_out, not_25_out, not_26_out, not_27_out, not_28_out, not_29_out, not_30_out, not_31_out,
       not_32_out, not_33_out, not_34_out, not_35_out, not_36_out, not_37_out, not_38_out, not_39_out,
       not_40_out, not_41_out, not_42_out, not_43_out, not_44_out;

  not not_1 (not_1_out, a1);
  and and_1 (and_1_out, not_1_out, not_2_out);
  not not_2 (not_2_out, a0);
  not not_3 (not_3_out, a3);
  and and_2 (and_2_out, not_3_out, not_4_out, a1_2);
  not not_4 (not_4_out, a1);
  not not_5 (not_5_out, a3);
  and and_3 (and_3_out, not_5_out, a1, a0);
  and and_4 (and_4_out, a3, not_6_out, not_7_out);
  not not_6 (not_6_out, a1);
  not not_7 (not_7_out, a1_2);
  and and_5 (and_5_out, a3, not_8_out);
  not not_8 (not_8_out, a0);
  and and_6 (and_6_out, a3, a1, a1_2);
  not not_9 (not_9_out, a3);
  and and_7 (and_7_out, not_9_out, not_10_out);
  not not_10 (not_10_out, a1);
  not not_11 (not_11_out, a3);
  and and_8 (and_8_out, not_11_out, not_12_out);
  not not_12 (not_12_out, a0);
  not not_13 (not_13_out, a1);
  and and_9 (and_9_out, not_13_out, not_14_out);
  not not_14 (not_14_out, a0);
  not not_15 (not_15_out, a3);
  and and_10 (and_10_out, not_15_out, a1_2);
  not not_16 (not_16_out, a1_2);
  and and_11 (and_11_out, a3, not_16_out, a0);
  not not_17 (not_17_out, a3);
  and and_12 (and_12_out, not_17_out, not_18_out);
  not not_18 (not_18_out, a1_2);
  not not_19 (not_19_out, a3);
  and and_13 (and_13_out, not_19_out, a0);
  not not_20 (not_20_out, a1_2);
  and and_14 (and_14_out, not_20_out, a0);
  not not_21 (not_21_out, a3);
  and and_15 (and_15_out, not_21_out, a1);
  and and_16 (and_16_out, a3, not_22_out);
  not not_22 (not_22_out, a1);
  not not_23 (not_23_out, a3);
  and and_17 (and_17_out, not_23_out, not_24_out, not_25_out);
  not not_24 (not_24_out, a1);
  not not_25 (not_25_out, a0);
  not not_26 (not_26_out, a1);
  and and_18 (and_18_out, not_26_out, a1_2, a0);
  and and_19 (and_19_out, a1, not_27_out, a0);
  not not_27 (not_27_out, a1_2);
  and and_20 (and_20_out, a1, a1_2, not_28_out);
  not not_28 (not_28_out, a0);
  and and_21 (and_21_out, a3, not_29_out, not_30_out);
  not not_29 (not_29_out, a1_2);
  not not_30 (not_30_out, a0);
  not not_31 (not_31_out, a1);
  and and_22 (and_22_out, not_31_out, not_32_out);
  not not_32 (not_32_out, a0);
  and and_23 (and_23_out, a1_2, not_33_out);
  not not_33 (not_33_out, a0);
  and and_24 (and_24_out, a3, a1_2);
  and and_25 (and_25_out, a3, a1);
  not not_34 (not_34_out, a1_2);
  and and_26 (and_26_out, not_34_out, not_35_out);
  not not_35 (not_35_out, a0);
  not not_36 (not_36_out, a3);
  and and_27 (and_27_out, not_36_out, a1, not_37_out);
  not not_37 (not_37_out, a1_2);
  and and_28 (and_28_out, a1, not_38_out);
  not not_38 (not_38_out, a0);
  and and_29 (and_29_out, a3, not_39_out);
  not not_39 (not_39_out, a1);
  and and_30 (and_30_out, a3, a1_2);
  not not_40 (not_40_out, a1);
  and and_31 (and_31_out, not_40_out, a1_2);
  and and_32 (and_32_out, a1_2, not_41_out);
  not not_41 (not_41_out, a0);
  not not_42 (not_42_out, a3);
  and and_33 (and_33_out, not_42_out, a1, not_43_out);
  not not_43 (not_43_out, a1_2);
  and and_34 (and_34_out, a3, not_44_out);
  not not_44 (not_44_out, a1);
  and and_35 (and_35_out, a3, a0);
  or or_1 (b, and_7_out, and_8_out, and_9_out, and_10_out, and_11_out);
  or or_2 (c, and_12_out, and_13_out, and_14_out, and_15_out, and_16_out);
  or or_3 (d, and_17_out, and_18_out, and_19_out, and_20_out, and_21_out);
  or or_4 (e, and_22_out, and_23_out, and_24_out, and_25_out);
  or or_5 (f, and_26_out, and_27_out, and_28_out, and_29_out, and_30_out);
  or or_6 (g, and_31_out, and_32_out, and_33_out, and_34_out, and_35_out);
  or or_7 (a, and_1_out, and_2_out, and_3_out, and_4_out, and_5_out, and_6_out);
endmodule
