// Logisim project EP_01_incompleto.circ as structural Verilog: 6 circuits, main circuit main
module main (
  input  a0,
  input  a1,
  input  a2,
  input  Ci,
  input  a3,
  input  b0,
  input  b1,
  input  b2,
  input  b3,
  output S0,
  output S1,
  output S2,
  output S3,
  output Co,
  output overflow
);

  soma4bits soma4bits_1 (
    .a1(a0), .b1(a1), .a2(a2), .b2(a3), .a4(b0), .b4(b1), .a8(b2), .b8(b3), .carry_in(Ci), .carry_out(Co),
    .S0(S0), .S1(S1), .S2(S2), .S3(S3), .overflow(overflow));
endmodule

module somaCompleta (
  input  a,
  input  b,
  input  carry_in,
  output S,
  output carry_out
);

  wire meiasoma_1_carry_out, meiasoma_1_s, meiasoma_2_carry_out;

  meiaSoma meiasoma_1 (.a(b), .b(a), .Carry_Out(meiasoma_1_carry_out), .S(meiasoma_1_s));
  meiaSoma meiasoma_2 (.a(meiasoma_1_s), .b(carry_in), .Carry_Out(meiasoma_2_carry_out), .S(S));
  or or_1 (carry_out, meiasoma_2_carry_out, meiasoma_1_carry_out);
endmodule

module meiaSoma (
  input  a,
  input  b,
  output S,
  output Carry_Out
);

  xor xor_1 (S, a, b);
  and and_1 (Carry_Out, a, b);
endmodule

module soma4bits (
  input  a1,
  input  b1,
  input  a2,
  input  b2,
  input  a4,
  input  b4,
  input  a8,
  input  b8,
  input  carry_in,
  output S0,
  output S1,
  output S2,
  output S3,
  output carry_out,
  output overflow
);

  wire soma2bits_1_carry_out;

  soma2bits soma2bits_1 (
    .a1(a1), .b1(b1), .a2(a2), .b2(b2), .carry_in(carry_in), .carry_out(soma2bits_1_carry_out), .S0(S0),
    .S1(S1));
  soma2bits soma2bits_2 (
    .a1(a4), .b1(b4), .a2(a8), .b2(b8), .carry_in(soma2bits_1_carry_out), .carry_out(carry_out), .S0(S2),
    .S1(S3));

  assign overflow = carry_out;
endmodule

module soma2bits (
  input  a1,
  input  b1,
  input  a2,
  input  b2,
  input  carry_in,
  output S0,
  output S1,
  output carry_out
);

  wire somacompleta_1_carry_out;

  somaCompleta somacompleta_1 (.a(a1), .b(b1), .carry_in(carry_in), .carry_out(somacompleta_1_carry_out), .S(S0));
  somaCompleta somacompleta_2 (.a(a2), .b(b2), .carry_in(somacompleta_1_carry_out), .carry_out(carry_out), .S(S1));
endmodule

module EP_01 (
  input  a0,
  input  a1,
  input  a2,
  input  Ci,
  input  a3,
  input  b0,
  input  b1,
  input  b2,
  input  b3,
  output S0,
  output S1,
  output S2,
  output S3,
  output Co,
  output overflow
);

  soma4bits soma4bits_1 (
    .a1(a0), .b1(a1), .a2(a2), .b2(a3), .a4(b0), .b4(b1), .a8(b2), .b8(b3), .carry_in(Ci), .carry_out(Co),
    .S0(S0), .S1(S1), .S2(S2), .S3(S3), .overflow(overflow));
endmodule
