// Logisim project EP_02pt1.circ as structural Verilog
module mux1 (
  input  E,
  input  a,
  input  b,
  output S
);

  wire and_1_out, and_2_out, not_1_out;

  not not_1 (not_1_out, E);
  and and_1 (and_1_out, E, b);
  and and_2 (and_2_out, not_1_out, a);
  or or_1 (S, and_2_out, and_1_out);
endmodule

module mux2 (
  input  E0,
  input  E1,
  input  a,
  input  b,
  input  c,
  input  d,
  output S
);

  wire and_1_out, and_2_out, and_3_out, and_4_out, not_1_out, not_2_out, not_3_out, not_4_out;

  not not_1 (not_1_out, E0);
  not not_2 (not_2_out, E1);
  and and_1 (and_1_out, a, not_1_out, not_2_out);
  not not_3 (not_3_out, E0);
  and and_2 (and_2_out, b, not_3_out, E1);
  not not_4 (not_4_out, E1);
  and and_3 (and_3_out, c, E0, not_4_out);
  and and_4 (and_4_out, d, E0, E1);
  or or_1 (S, and_1_out, and_2_out, and_3_out, and_4_out);
endmodule

module ULA_1 (
  input  Bi,
  input  a,
  input  b,
  input  Ci,
  input  op0,
  input  op1,
  output S,
  output Ci_2
);

  wire and_1_out, mux1_1_s, not_1_out, not_2_out, or_1_out, somacompleta_1_s;

  not not_1 (not_1_out, b);
  mux1 mux1_1 (.a(b), .b(not_1_out), .E(Bi), .S(mux1_1_s));
  and and_1 (and_1_out, a, mux1_1_s);
  or or_1 (or_1_out, a, mux1_1_s);
  not not_2 (not_2_out, a);
  somaCompleta somacompleta_1 (.a(a), .b(mux1_1_s), .carry_in(Ci), .carry_out(Ci_2), .S(somacompleta_1_s));
  mux2 mux2_1 (.a(and_1_out), .b(or_1_out), .c(not_2_out), .d(somacompleta_1_s), .E0(op0), .E1(op1), .S(S));
endmodule

module ULA_4 (
  input  Bi,
  input  OP0,
  input  OP1,
  input  b3,
  input  b2,
  input  b1,
  input  b0,
  input  a3,
  input  a2,
  input  a1,
  input  a0,
  output S0,
  output S1,
  output S2,
  output S3,
  output Co
);

  wire ula_1_1_ci_2, ula_1_2_ci_2, ula_1_3_ci_2;

  ULA_1 ula_1_1 (.Bi(Bi), .a(a0), .b(b0), .Ci(Bi), .op0(OP0), .op1(OP1), .S(S0), .Ci_2(ula_1_1_ci_2));
  ULA_1 ula_1_2 (.Bi(Bi), .a(a1), .b(b1), .Ci(ula_1_1_ci_2), .op0(OP0), .op1(OP1), .S(S1), .Ci_2(ula_1_2_ci_2));
  ULA_1 ula_1_3 (.Bi(Bi), .a(a2), .b(b2), .Ci(ula_1_2_ci_2), .op0(OP0), .op1(OP1), .S(S2), .Ci_2(ula_1_3_ci_2));
  ULA_1 ula_1_4 (.Bi(Bi), .a(a3), .b(b3), .Ci(ula_1_3_ci_2), .op0(OP0), .op1(OP1), .S(S3), .Ci_2(Co));
endmodule
