// Logisim project q4c.circ as structural Verilog: 1 circuit, main circuit main
module main (
  input  a,
  input  b,
  input  c
);

  wire and_1_out, not_1_out, not_2_out, or_1_out;

  not not_1 (not_1_out, a);
  and and_1 (and_1_out, not_1_out, not_2_out);
  not not_2 (not_2_out, c);
  or or_1 (or_1_out, a, and_1_out);
  // Probe on or_1_out

  // Notes on the sheet:
  //   Arthur Goncalves De Moraes 816479 q4c
endmodule
