// Logisim project q4e.circ as structural Verilog: 1 circuit, main circuit main
module main (
  input  a,
  input  b,
  input  c
);

  wire and_1_out, and_2_out, and_3_out, not_1_out, not_2_out, or_1_out;

  not not_1 (not_1_out, a);
  not not_2 (not_2_out, b);
  and and_1 (and_1_out, not_1_out, c);
  and and_2 (and_2_out, not_2_out, c);
  and and_3 (and_3_out, c, a, b);
  or or_1 (or_1_out, and_1_out, and_2_out, and_3_out);
  // Probe on or_1_out

  // Notes on the sheet:
  //   Arthur Goncalves de Moraes 816479 q4e
endmodule
