// Logisim project q5b.circ as structural Verilog: 1 circuit, main circuit main
module main (
  input  a,
  input  b,
  input  c
);

  wire nor_1_out, nor_2_out, nor_3_out, nor_4_out, nor_5_out, nor_6_out, nor_7_out;

  nor nor_1 (nor_1_out, c, c);
  nor nor_2 (nor_2_out, a, b, nor_1_out);
  nor nor_3 (nor_3_out, a, a);
  nor nor_4 (nor_4_out, c, c);
  nor nor_5 (nor_5_out, nor_3_out, b, nor_4_out);
  nor nor_6 (nor_6_out, nor_5_out, nor_2_out);
  nor nor_7 (nor_7_out, nor_6_out, nor_6_out);
  // Probe on nor_7_out

  // Notes on the sheet:
  //   Arthur Goncalves de Moraes 816479 q5b
  //   A'.B.'C
  //   AB'C
endmodule
